# Fritzing sketch G-Bag (saved by Fritzing 0.9.4)
breadboards: 1

parts:
  부품1 = Arduino Uno (Rev3)
  S1 = Toggle Switch [package=THT]
  R1 = Resistor [tolerance=±5% resistance=220 package=THT]
  R2 = Resistor [tolerance=±5% resistance=220 package=THT]
  ANT1 = Antenna
  Part1 = Solar Cell
  U1 = LIPO-2000mAh [package=lipo-2000]

nets (from the breadboard view):
  N1: 부품1.A1, ANT1.antenna_lead
  N2: 부품1.D6_PWM, S1.L2, R2.Pin_1
  N3: 부품1.D7, S1.L1, R1.Pin_1
  N4: 부품1.3V3, S1.COM
  N5: 부품1.5V, Part1.+, U1.+
  N6: 부품1.GND, R1.Pin_0, R2.Pin_0, Part1.-, U1.-
